# Fritzing sketch Solarstation (saved by Fritzing 0.9.4)

parts:
  U1 = NodeMCU V1.0
  Part1 = Voltage Sensor 25V
  In_5V;_Out_~3_3V = Mini-360 DC-DC Buck converter [package=THT]
  Part2 = Analog Digital MUX Breakout
  Solar = Screw terminal - 2 pins [package=THT]
  Battery = Screw terminal - 2 pins [package=THT]
  Load = Screw terminal - 2 pins [package=THT]
  Part3 = Solar Cell
  BAT1 = 12 battery [package=battery]
  Part4 = Voltage Sensor 25V
  Part5 = Voltage Sensor 25V
  ACS712_Current_Sensor4 = ACS712 Current Sensor
  ACS712_Current_Sensor5 = ACS712 Current Sensor
  ACS712_Current_Sensor6 = ACS712 Current Sensor
  12V_Consumer = Screw terminal - 2 pins [package=THT]

nets:
  N1: U1.D0, Part2.S0
  N2: U1.D1, Part2.S1
  N3: U1.D2, Part2.S2
  N4: U1.D3, Part2.S3
  GND: U1.GND, In_5V;_Out_~3_3V.IN-, Part2.GND
  3V3: U1.3V3, Part2.VCC
  N5: U1.Vin, In_5V;_Out_~3_3V.IN+
  N6: U1.A0, Part2.SIG
  N7: Part1.GND, Solar.pin2, Part3.-
  N8: Part1.VCC, Part1.+, Solar.pin1, ACS712_Current_Sensor4.Plus
  N9: Part1.S, Part2.C0
  GND_2: Part1.-, In_5V;_Out_~3_3V.OUT-, Part4.-, Part5.-, ACS712_Current_Sensor5.GND, ACS712_Current_Sensor6.GND
  VCC: In_5V;_Out_~3_3V.OUT+, ACS712_Current_Sensor4.VCC, ACS712_Current_Sensor5.VCC, ACS712_Current_Sensor6.VCC
  N10: Part2.C1, ACS712_Current_Sensor4.OUT
  N11: Part2.C2, Part5.S
  N12: Part2.C3, ACS712_Current_Sensor6.OUT
  N13: Part2.C4, Part4.S
  N14: Part2.C5, ACS712_Current_Sensor5.OUT
  N15: Battery.pin1, Part5.VCC, ACS712_Current_Sensor6.Minus
  N16: Battery.pin2, BAT1.-, Part5.GND
  N17: Load.pin1, Part4.VCC, ACS712_Current_Sensor5.Minus
  N18: Load.pin2, Part4.GND, 12V_Consumer.pin2
  N19: Part3.+, ACS712_Current_Sensor4.Minus
  N20: BAT1.+, ACS712_Current_Sensor6.Plus
  N21: ACS712_Current_Sensor5.Plus, 12V_Consumer.pin1

custom parts:
  NodeMCU V1.0: ESP8266 based NodeMCU
  Mini-360 DC-DC Buck converter: Mini-360 DC-DC Buck converter. Tiny buck step down voltage converter, input voltage 4.75 to 23V output 1 to 17V adjustable. Available from ebay and the like.
  12 battery: 12V lead acid type battery, like the Husqvarna YTH2448 12V 35AH battery. This is the mini version 1/4 the size of the actual battery to be closer to typical breadboard parts (around 2in wide rathher than 7in). The pads in pcb are sized to accomidate up to 14ga wire (as these batterys will deliver high currents.)
  ACS712 Current Sensor: A breakout board for the Allegro ACS712 is a Hall Effect-based linear current sensor. The module operates at 5V.
